// Logisim project lab1_part1.circ as structural Verilog: 3 circuits, main circuit main
module main (
  input  x,
  input  y,
  input  s,
  output f
);

  wire n7408_1_pin2, n7408_1_pin3, n7408_1_pin7, n7408_1_pin14, n7408_2_pin3;

  _7408 #(.ShowInternalStructure("true"), .VccGndPorts("true")) u_7408_1 (
    .pin1(x), .pin2(n7408_1_pin2), .pin3(n7408_1_pin3), .pin7(n7408_1_pin7), .pin14(n7408_1_pin14));  // open: pin4, pin5, pin6, pin13, pin12, pin11, pin10, pin9, pin8
  _7404 #(.ShowInternalStructure("true"), .VccGndPorts("true")) u_7404_1 (
    .pin1(s), .pin2(n7408_1_pin2), .pin7(n7408_1_pin7), .pin14(n7408_1_pin14));  // open: pin3, pin4, pin5, pin6, pin13, pin12, pin11, pin10, pin9, pin8
  _7408 #(.ShowInternalStructure("true"), .VccGndPorts("true")) u_7408_2 (
    .pin1(y), .pin2(s), .pin3(n7408_2_pin3), .pin7(n7408_1_pin7), .pin14(n7408_1_pin14));  // open: pin4, pin5, pin6, pin13, pin12, pin11, pin10, pin9, pin8
  _7432 #(.ShowInternalStructure("true"), .VccGndPorts("true")) u_7432_1 (
    .pin1(n7408_2_pin3), .pin2(n7408_1_pin3), .pin3(f), .pin7(n7408_1_pin7), .pin14(n7408_1_pin14));  // open: pin4, pin5, pin6, pin13, pin12, pin11, pin10, pin9, pin8
  // also tied to GND on the sheet: n7408_1_pin7
  // also tied to VCC on the sheet: n7408_1_pin14
endmodule

module cheaper (
  input  x,
  input  y,
  input  s,
  output f
);

  wire n7408_1_pin2, n7408_1_pin3, n7408_1_pin6, n7408_1_pin7, n7408_1_pin14;

  _7408 #(.ShowInternalStructure("true"), .VccGndPorts("true")) u_7408_1 (
    .pin1(x), .pin2(n7408_1_pin2), .pin3(n7408_1_pin3), .pin4(y), .pin5(s), .pin6(n7408_1_pin6),
    .pin7(n7408_1_pin7), .pin14(n7408_1_pin14));  // open: pin13, pin12, pin11, pin10, pin9, pin8
  _7404 #(.ShowInternalStructure("true"), .VccGndPorts("true")) u_7404_1 (
    .pin1(s), .pin2(n7408_1_pin2), .pin7(n7408_1_pin7), .pin14(n7408_1_pin14));  // open: pin3, pin4, pin5, pin6, pin13, pin12, pin11, pin10, pin9, pin8
  _7432 #(.ShowInternalStructure("true"), .VccGndPorts("true")) u_7432_1 (
    .pin1(n7408_1_pin6), .pin2(n7408_1_pin3), .pin3(f), .pin7(n7408_1_pin7), .pin14(n7408_1_pin14));  // open: pin4, pin5, pin6, pin13, pin12, pin11, pin10, pin9, pin8
  // also tied to GND on the sheet: n7408_1_pin7
  // also tied to VCC on the sheet: n7408_1_pin14
endmodule

module cheapest (
  input  x,
  input  y,
  input  s,
  output f
);

  wire n7404_1_pin2, n7404_1_pin3, n7404_1_pin4, n7404_1_pin6, n7404_1_pin7, n7404_1_pin10, n7404_1_pin11,
       n7404_1_pin12, n7404_1_pin14;

  _7404 #(.ShowInternalStructure("true"), .VccGndPorts("true")) u_7404_1 (
    .pin1(x), .pin2(n7404_1_pin2), .pin3(n7404_1_pin3), .pin4(n7404_1_pin4), .pin5(s), .pin6(n7404_1_pin6),
    .pin7(n7404_1_pin7), .pin14(n7404_1_pin14), .pin13(y), .pin12(n7404_1_pin12), .pin11(n7404_1_pin11),
    .pin10(n7404_1_pin10));  // open: pin9, pin8
  _7432 #(.ShowInternalStructure("true"), .VccGndPorts("true")) u_7432_1 (
    .pin1(n7404_1_pin2), .pin2(s), .pin3(n7404_1_pin3), .pin4(n7404_1_pin4), .pin5(n7404_1_pin10), .pin6(f),
    .pin7(n7404_1_pin7), .pin14(n7404_1_pin14), .pin13(n7404_1_pin12), .pin12(n7404_1_pin6),
    .pin11(n7404_1_pin11));  // open: pin10, pin9, pin8
  // also tied to GND on the sheet: n7404_1_pin7
  // also tied to VCC on the sheet: n7404_1_pin14
endmodule
