// Logisim project lab1_part2.circ as structural Verilog: 2 circuits, main circuit main
module main (
  input  a,
  input  b,
  input  c,
  output f
);

  wire n7404_1_pin12, n7404_2_pin2, n7408_1_pin11, n7432_1_pin3, n7432_1_pin7, n7432_1_pin14;

  _7432 #(.ShowInternalStructure("true"), .VccGndPorts("true")) u_7432_1 (
    .pin1(a), .pin2(b), .pin3(n7432_1_pin3), .pin7(n7432_1_pin7), .pin14(n7432_1_pin14));  // open: pin4, pin5, pin6, pin13, pin12, pin11, pin10, pin9, pin8
  _7404 #(.ShowInternalStructure("true"), .VccGndPorts("true")) u_7404_1 (
    .pin7(n7432_1_pin7), .pin14(n7432_1_pin14), .pin13(b), .pin12(n7404_1_pin12));  // open: pin1, pin2, pin3, pin4, pin5, pin6, pin11, pin10, pin9, pin8
  _7404 #(.ShowInternalStructure("true"), .VccGndPorts("true")) u_7404_2 (
    .pin1(n7432_1_pin3), .pin2(n7404_2_pin2), .pin7(n7432_1_pin7), .pin14(n7432_1_pin14));  // open: pin3, pin4, pin5, pin6, pin13, pin12, pin11, pin10, pin9, pin8
  _7408 #(.ShowInternalStructure("true"), .VccGndPorts("true")) u_7408_1 (
    .pin7(n7432_1_pin7), .pin14(n7432_1_pin14), .pin13(c), .pin12(n7404_1_pin12), .pin11(n7408_1_pin11));  // open: pin1, pin2, pin3, pin4, pin5, pin6, pin10, pin9, pin8
  _7432 #(.ShowInternalStructure("true"), .VccGndPorts("true")) u_7432_2 (
    .pin7(n7432_1_pin7), .pin14(n7432_1_pin14), .pin13(n7408_1_pin11), .pin12(n7404_2_pin2), .pin11(f));  // open: pin1, pin2, pin3, pin4, pin5, pin6, pin10, pin9, pin8
  // also tied to GND on the sheet: n7432_1_pin7
  // also tied to VCC on the sheet: n7432_1_pin14
endmodule

module cheaper (
  input  a,
  input  b,
  input  c,
  output f
);

  wire n7432_1_pin3, n7432_1_pin4, n7432_1_pin5, n7432_1_pin7, n7432_1_pin11, n7432_1_pin12, n7432_1_pin14;

  _7432 #(.ShowInternalStructure("true"), .VccGndPorts("true")) u_7432_1 (
    .pin1(a), .pin2(b), .pin3(n7432_1_pin3), .pin4(n7432_1_pin4), .pin5(n7432_1_pin5), .pin6(f),
    .pin7(n7432_1_pin7), .pin14(n7432_1_pin14), .pin13(b), .pin12(n7432_1_pin12), .pin11(n7432_1_pin11));  // open: pin10, pin9, pin8
  _7404 #(.ShowInternalStructure("true"), .VccGndPorts("true")) u_7404_1 (
    .pin1(n7432_1_pin3), .pin2(n7432_1_pin5), .pin7(n7432_1_pin7), .pin14(n7432_1_pin14), .pin13(c),
    .pin12(n7432_1_pin12), .pin11(n7432_1_pin11), .pin10(n7432_1_pin4));  // open: pin3, pin4, pin5, pin6, pin9, pin8
  // also tied to GND on the sheet: n7432_1_pin7
  // also tied to VCC on the sheet: n7432_1_pin14
endmodule
