// Logisim project lab2_part1.circ as structural Verilog: 3 circuits, main circuit main
module main (
  input  in_1,
  input  in_2,
  input  in_3,
  input  in_4,
  input  in_5,
  input  in_6,
  output out_7
);

  mux4to1 mux4to1_1 (.x(in_1), .w(in_2), .s0(in_3), .s1(in_4), .v(in_5), .u(in_6), .out_7(out_7));
endmodule

module mux2to1 (
  input  x,
  input  y,
  input  s,
  output f
);

  wire and_1_out, and_2_out, not_1_out;

  not not_1 (not_1_out, s);
  and and_1 (and_1_out, x, s);
  and and_2 (and_2_out, y, not_1_out);
  or or_1 (f, and_1_out, and_2_out);
endmodule

module mux4to1 (
  input  x,
  input  w,
  input  s0,
  input  s1,
  input  v,
  input  u,
  output out_7
);

  wire mux2to1_1_f, mux2to1_2_f;

  mux2to1 mux2to1_1 (.x(x), .y(w), .s(s0), .f(mux2to1_1_f));
  mux2to1 mux2to1_2 (.x(v), .y(u), .s(s0), .f(mux2to1_2_f));
  mux2to1 mux2to1_3 (.x(mux2to1_1_f), .y(mux2to1_2_f), .s(s1), .f(out_7));
endmodule
