// Logisim project lab3.circ as structural Verilog: 18 circuits, main circuit main
module main (
  input  [3:0] A,
  input  [3:0] B,
  input  [2:0] op
);

  wire hex_decoder_1_s0, hex_decoder_1_s1, hex_decoder_1_s2, hex_decoder_1_s3, hex_decoder_1_s4,
       hex_decoder_1_s5, hex_decoder_1_s6, hex_decoder_2_s0, hex_decoder_2_s1, hex_decoder_2_s2,
       hex_decoder_2_s3, hex_decoder_2_s4, hex_decoder_2_s5, hex_decoder_2_s6, hex_decoder_3_s0,
       hex_decoder_3_s1, hex_decoder_3_s2, hex_decoder_3_s3, hex_decoder_3_s4, hex_decoder_3_s5,
       hex_decoder_3_s6, hex_decoder_4_s0, hex_decoder_4_s1, hex_decoder_4_s2, hex_decoder_4_s3,
       hex_decoder_4_s4, hex_decoder_4_s5, hex_decoder_4_s6;
  wire [7:0] alu_1_out_4;

  HEX_DECODER hex_decoder_1 (
    .SW0(A), .S6(hex_decoder_1_s6), .S5(hex_decoder_1_s5), .S0(hex_decoder_1_s0), .S1(hex_decoder_1_s1),
    .S4(hex_decoder_1_s4), .S3(hex_decoder_1_s3), .S2(hex_decoder_1_s2));
  HEX_DECODER hex_decoder_2 (
    .SW0(B), .S6(hex_decoder_2_s6), .S5(hex_decoder_2_s5), .S0(hex_decoder_2_s0), .S1(hex_decoder_2_s1),
    .S4(hex_decoder_2_s4), .S3(hex_decoder_2_s3), .S2(hex_decoder_2_s2));
  _7_Segment_Display HEXA (
    .g(hex_decoder_1_s6), .f(hex_decoder_1_s5), .a(hex_decoder_1_s0), .b(hex_decoder_1_s1),
    .e(hex_decoder_1_s4), .d(hex_decoder_1_s3), .c(hex_decoder_1_s2));  // open: dp
  _7_Segment_Display HEXB (
    .g(hex_decoder_2_s6), .f(hex_decoder_2_s5), .a(hex_decoder_2_s0), .b(hex_decoder_2_s1),
    .e(hex_decoder_2_s4), .d(hex_decoder_2_s3), .c(hex_decoder_2_s2));  // open: dp
  ALU alu_1 (.A(A), .B(B), .op(op), .out_4(alu_1_out_4));
  HEX_DECODER hex_decoder_3 (
    .SW0(alu_1_out_4[3:0]), .S6(hex_decoder_3_s6), .S5(hex_decoder_3_s5), .S0(hex_decoder_3_s0),
    .S1(hex_decoder_3_s1), .S4(hex_decoder_3_s4), .S3(hex_decoder_3_s3), .S2(hex_decoder_3_s2));
  HEX_DECODER hex_decoder_4 (
    .SW0(alu_1_out_4[7:4]), .S6(hex_decoder_4_s6), .S5(hex_decoder_4_s5), .S0(hex_decoder_4_s0),
    .S1(hex_decoder_4_s1), .S4(hex_decoder_4_s4), .S3(hex_decoder_4_s3), .S2(hex_decoder_4_s2));
  _7_Segment_Display HEXALU1 (
    .g(hex_decoder_4_s6), .f(hex_decoder_4_s5), .a(hex_decoder_4_s0), .b(hex_decoder_4_s1),
    .e(hex_decoder_4_s4), .d(hex_decoder_4_s3), .c(hex_decoder_4_s2));  // open: dp
  _7_Segment_Display HEXALU0 (
    .g(hex_decoder_3_s6), .f(hex_decoder_3_s5), .a(hex_decoder_3_s0), .b(hex_decoder_3_s1),
    .e(hex_decoder_3_s4), .d(hex_decoder_3_s3), .c(hex_decoder_3_s2));  // open: dp
endmodule

module full_adder (
  input  Cin,
  input  A,
  input  B,
  output Cout,
  output S
);

  wire and_1_out, and_2_out, xor_1_out;

  and and_1 (and_1_out, B, A);
  xor xor_1 (xor_1_out, A, B);
  and and_2 (and_2_out, xor_1_out, Cin);
  xor xor_2 (S, Cin, xor_1_out);
  or or_1 (Cout, and_2_out, and_1_out);
endmodule

module ripple_carry4 (
  input  [3:0] A,
  input  [3:0] B,
  input  Cin,
  output Cout,
  output [3:0] S
);

  wire full_adder_1_cout, full_adder_2_cout, full_adder_3_cout;

  full_adder full_adder_1 (.Cin(Cin), .A(A[0]), .B(B[0]), .Cout(full_adder_1_cout), .S(S[0]));
  full_adder full_adder_2 (.Cin(full_adder_1_cout), .A(A[1]), .B(B[1]), .Cout(full_adder_2_cout), .S(S[1]));
  full_adder full_adder_3 (.Cin(full_adder_2_cout), .A(A[2]), .B(B[2]), .Cout(full_adder_3_cout), .S(S[2]));
  full_adder full_adder_4 (.Cin(full_adder_3_cout), .A(A[3]), .B(B[3]), .Cout(Cout), .S(S[3]));
endmodule

module op0 (
  input  [3:0] A,
  output [7:0] ALUout
);

  wire full_adder_1_cout, full_adder_2_cout, full_adder_3_cout, full_adder_4_cout, full_adder_5_cout,
       full_adder_6_cout, full_adder_7_cout;

  full_adder full_adder_1 (.Cin(1'b1), .A(A[0]), .Cout(full_adder_1_cout), .S(ALUout[0]));  // open: B
  full_adder full_adder_2 (.Cin(full_adder_1_cout), .A(A[1]), .Cout(full_adder_2_cout), .S(ALUout[1]));  // open: B
  full_adder full_adder_3 (.Cin(full_adder_2_cout), .A(A[2]), .Cout(full_adder_3_cout), .S(ALUout[2]));  // open: B
  full_adder full_adder_4 (.Cin(full_adder_3_cout), .A(A[3]), .Cout(full_adder_4_cout), .S(ALUout[3]));  // open: B
  full_adder full_adder_5 (.Cin(full_adder_4_cout), .Cout(full_adder_5_cout), .S(ALUout[4]));  // open: A, B
  full_adder full_adder_6 (.Cin(full_adder_5_cout), .Cout(full_adder_6_cout), .S(ALUout[5]));  // open: A, B
  full_adder full_adder_7 (.Cin(full_adder_6_cout), .Cout(full_adder_7_cout), .S(ALUout[6]));  // open: A, B
  full_adder full_adder_8 (.Cin(full_adder_7_cout), .Cout(ALUout[7]));  // open: A, B, S
endmodule

module op1 (
  input  [3:0] A,
  input  [3:0] B,
  output [7:0] ALUout
);

  wire full_adder_1_cout, full_adder_2_cout, full_adder_3_cout, full_adder_4_cout, full_adder_5_cout,
       full_adder_6_cout, full_adder_7_cout;

  full_adder full_adder_1 (.A(A[0]), .B(B[0]), .Cout(full_adder_1_cout), .S(ALUout[0]));  // open: Cin
  full_adder full_adder_2 (.Cin(full_adder_1_cout), .A(A[1]), .B(B[1]), .Cout(full_adder_2_cout), .S(ALUout[1]));
  full_adder full_adder_3 (.Cin(full_adder_2_cout), .A(A[2]), .B(B[2]), .Cout(full_adder_3_cout), .S(ALUout[2]));
  full_adder full_adder_4 (.Cin(full_adder_3_cout), .A(A[3]), .B(B[3]), .Cout(full_adder_4_cout), .S(ALUout[3]));
  full_adder full_adder_5 (.Cin(full_adder_4_cout), .Cout(full_adder_5_cout), .S(ALUout[4]));  // open: A, B
  full_adder full_adder_6 (.Cin(full_adder_5_cout), .Cout(full_adder_6_cout), .S(ALUout[5]));  // open: A, B
  full_adder full_adder_7 (.Cin(full_adder_6_cout), .Cout(full_adder_7_cout), .S(ALUout[6]));  // open: A, B
  full_adder full_adder_8 (.Cin(full_adder_7_cout), .S(ALUout[7]));  // open: A, B, Cout
endmodule

module op2 (
  input  [3:0] A,
  input  [3:0] B,
  output [7:0] ALUout
);

  wire [7:0] bit_extender_1_out, bit_extender_2_out;

  assign bit_extender_1_out = {{4{1'b0}}, A};  // Bit_Extender bit_extender_1
  assign bit_extender_2_out = {{4{1'b0}}, B};  // Bit_Extender bit_extender_2
  Adder adder_1 (.a(bit_extender_1_out), .b(bit_extender_2_out), .out(ALUout));  // open: cin, cout
endmodule

module op3 (
  input  [3:0] A,
  input  [3:0] B,
  output [7:0] ALUout
);

  or or_1 (ALUout[4], A[0], B[0]);
  xor xor_1 (ALUout[0], A[0], B[0]);
  or or_2 (ALUout[5], A[1], B[1]);
  xor xor_2 (ALUout[1], A[1], B[1]);
  or or_3 (ALUout[6], A[2], B[2]);
  xor xor_3 (ALUout[2], A[2], B[2]);
  or or_4 (ALUout[7], A[3], B[3]);
  xor xor_4 (ALUout[3], A[3], B[3]);
endmodule

module op4 (
  input  [3:0] A,
  input  [3:0] B,
  output [7:0] ALUout
);

  or or_1 (ALUout[0], A[0], A[1], A[2], A[3], B[0], B[1], B[2], B[3]);

  assign ALUout[7:1] = {7{1'b0}};
endmodule

module op5 (
  input  [3:0] A,
  input  [3:0] B,
  output [7:0] ALUout
);


  assign ALUout = {A, B};
endmodule

module ALU (
  input  [3:0] A,
  input  [3:0] B,
  input  [2:0] op,
  output [7:0] out_4
);

  wire [7:0] op0_1_aluout, op1_1_aluout, op2_1_aluout, op3_1_aluout, op4_1_aluout, op5_1_aluout;

  op0 op0_1 (.A(A), .ALUout(op0_1_aluout));
  op1 op1_1 (.A(A), .B(B), .ALUout(op1_1_aluout));
  op2 op2_1 (.A(A), .B(B), .ALUout(op2_1_aluout));
  op3 op3_1 (.A(A), .B(B), .ALUout(op3_1_aluout));
  op4 op4_1 (.A(A), .B(B), .ALUout(op4_1_aluout));
  op5 op5_1 (.A(A), .B(B), .ALUout(op5_1_aluout));
  Multiplexer #(.enable("false"), .select(3), .width(8)) multiplexer_1 (
    .in0(op0_1_aluout), .in1(op1_1_aluout), .in2(op2_1_aluout), .in3(op3_1_aluout), .in4(op4_1_aluout),
    .in5(op5_1_aluout), .out(out_4), .sel(op));  // open: in6, in7
endmodule

module HEX0 (
  input  D3,
  input  D2,
  input  D1,
  input  D0,
  output S0
);

  wire and_1_out, and_2_out, and_3_out, and_4_out, and_5_out, not_1_out, not_2_out, not_3_out, not_4_out;

  not not_1 (not_1_out, D3);
  not not_2 (not_2_out, D2);
  not not_3 (not_3_out, D1);
  not not_4 (not_4_out, D0);
  and and_1 (and_1_out, not_2_out, not_4_out);
  and and_2 (and_2_out, not_1_out, D1);
  and and_3 (and_3_out, not_1_out, D2, D0);
  and and_4 (and_4_out, D2, D1);
  and and_5 (and_5_out, D3, not_2_out, not_3_out);
  or or_1 (S0, and_1_out, and_2_out, and_3_out, and_4_out, and_5_out);
endmodule

module HEX1 (
  input  D3,
  input  D2,
  input  D1,
  input  D0,
  output S1
);

  wire and_1_out, and_2_out, and_3_out, and_4_out, and_5_out, not_1_out, not_2_out, not_3_out, not_4_out;

  not not_1 (not_1_out, D3);
  not not_2 (not_2_out, D2);
  not not_3 (not_3_out, D1);
  not not_4 (not_4_out, D0);
  and and_1 (and_1_out, not_1_out, not_2_out);
  and and_2 (and_2_out, not_1_out, not_3_out, not_4_out);
  and and_3 (and_3_out, not_2_out, not_4_out);
  and and_4 (and_4_out, not_1_out, D1, D0);
  and and_5 (and_5_out, D3, not_3_out, D0);
  or or_1 (S1, and_1_out, and_2_out, and_3_out, and_4_out, and_5_out);
endmodule

module HEX2 (
  input  D3,
  input  D2,
  input  D1,
  input  D0,
  output S2
);

  wire and_1_out, and_2_out, and_3_out, and_4_out, and_5_out, not_1_out, not_2_out, not_3_out;

  not not_1 (not_1_out, D3);
  not not_2 (not_2_out, D2);
  not not_3 (not_3_out, D1);
  and and_1 (and_1_out, not_1_out, not_3_out);
  and and_2 (and_2_out, not_1_out, D0);
  and and_3 (and_3_out, not_3_out, D0);
  and and_4 (and_4_out, not_1_out, D2);
  and and_5 (and_5_out, D3, not_2_out);
  or or_1 (S2, and_1_out, and_2_out, and_3_out, and_4_out, and_5_out);
endmodule

module HEX3 (
  input  D3,
  input  D2,
  input  D1,
  input  D0,
  output S3
);

  wire and_1_out, and_2_out, and_3_out, and_4_out, and_5_out, and_6_out, not_1_out, not_2_out, not_3_out,
       not_4_out;

  not not_1 (not_1_out, D3);
  not not_2 (not_2_out, D2);
  not not_3 (not_3_out, D1);
  not not_4 (not_4_out, D0);
  and and_1 (and_1_out, not_1_out, not_2_out, not_4_out);
  and and_2 (and_2_out, not_1_out, D1, not_4_out);
  and and_3 (and_3_out, not_2_out, D1, D0);
  and and_4 (and_4_out, D2, not_3_out, D0);
  and and_5 (and_5_out, D3, not_3_out);
  and and_6 (and_6_out, D3, D2, not_4_out);
  or or_1 (S3, and_1_out, and_2_out, and_3_out, and_4_out, and_5_out, and_6_out);
endmodule

module HEX4 (
  input  D3,
  input  D2,
  input  D1,
  input  D0,
  output S4
);

  wire and_1_out, and_2_out, and_3_out, and_4_out, not_1_out, not_2_out;

  not not_1 (not_1_out, D2);
  not not_2 (not_2_out, D0);
  and and_1 (and_1_out, not_1_out, not_2_out);
  and and_2 (and_2_out, D1, not_2_out);
  and and_3 (and_3_out, D3, D1);
  and and_4 (and_4_out, D3, D2);
  or or_1 (S4, and_1_out, and_2_out, and_3_out, and_4_out);
endmodule

module HEX5 (
  input  D3,
  input  D2,
  input  D1,
  input  D0,
  output S5
);

  wire and_1_out, and_2_out, and_3_out, and_4_out, and_5_out, not_1_out, not_2_out, not_3_out, not_4_out;

  not not_1 (not_1_out, D3);
  not not_2 (not_2_out, D2);
  not not_3 (not_3_out, D1);
  not not_4 (not_4_out, D0);
  and and_1 (and_1_out, not_1_out, not_3_out, not_4_out);
  and and_2 (and_2_out, not_1_out, D2, not_3_out);
  and and_3 (and_3_out, not_1_out, D2, not_4_out);
  and and_4 (and_4_out, D3, not_2_out);
  and and_5 (and_5_out, D3, D1);
  or or_1 (S5, and_1_out, and_2_out, and_3_out, and_4_out, and_5_out);
endmodule

module HEX6 (
  input  D3,
  input  D2,
  input  D1,
  input  D0,
  output S6
);

  wire and_1_out, and_2_out, and_3_out, not_1_out, not_2_out, not_3_out;

  not not_1 (not_1_out, D2);
  not not_2 (not_2_out, D1);
  not not_3 (not_3_out, D0);
  and and_1 (and_1_out, not_1_out, D1);
  and and_2 (and_2_out, D2, not_2_out);
  and and_3 (and_3_out, D2, not_3_out);
  or or_1 (S6, and_1_out, and_2_out, and_3_out, D3);
endmodule

module HEX_DECODER (
  input  [3:0] SW0,
  output S6,
  output S5,
  output S0,
  output S1,
  output S4,
  output S3,
  output S2
);

  HEX4 hex4_1 (.D3(SW0[3]), .D2(SW0[2]), .D1(SW0[1]), .D0(SW0[0]), .S4(S4));
  HEX6 hex6_1 (.D3(SW0[3]), .D2(SW0[2]), .D1(SW0[1]), .D0(SW0[0]), .S6(S6));
  HEX3 hex3_1 (.D3(SW0[3]), .D2(SW0[2]), .D1(SW0[1]), .D0(SW0[0]), .S3(S3));
  HEX5 hex5_1 (.D3(SW0[3]), .D2(SW0[2]), .D1(SW0[1]), .D0(SW0[0]), .S5(S5));
  HEX2 hex2_1 (.D3(SW0[3]), .D2(SW0[2]), .D1(SW0[1]), .D0(SW0[0]), .S2(S2));
  HEX0 hex0_1 (.D3(SW0[3]), .D2(SW0[2]), .D1(SW0[1]), .D0(SW0[0]), .S0(S0));
  HEX1 hex1_1 (.D3(SW0[3]), .D2(SW0[2]), .D1(SW0[1]), .D0(SW0[0]), .S1(S1));
endmodule
