// Logisim project Latches_and_FlipFlops.circ as structural Verilog
module SRLatchNAND (
  input  S,
  input  R,
  output out_3,
  output out_4
);

  nand nand_1 (out_3, S, out_4);
  nand nand_2 (out_4, out_3, R);
endmodule

module FbAND (
  input  in_1,
  output out_2
);

  and and_1 (out_2, in_1, out_2);
endmodule

module FbOR (
  input  in_1,
  output out_2
);

  or or_1 (out_2, in_1, out_2);
endmodule

module FbNAND (
  input  in_1,
  output out_2
);

  nand nand_1 (out_2, in_1, out_2);
endmodule

module FbNOR (
  input  in_1,
  output out_2
);

  nor nor_1 (out_2, in_1, out_2);
endmodule

module ClockedSRLatch (
  input  S,
  input  Clk,
  input  R,
  output Q,
  output Qcomp
);

  wire nand_1_out, nand_2_out;

  nand nand_1 (nand_1_out, S, Clk);
  nand nand_2 (nand_2_out, Clk, R);
  nand nand_3 (Q, nand_1_out, Qcomp);
  nand nand_4 (Qcomp, Q, nand_2_out);
endmodule

module DLatch (
  input  D,
  input  Clk,
  output Q,
  output Qcomp
);

  wire nand_1_out, nand_2_out, not_1_out;

  not not_1 (not_1_out, D);
  nand nand_1 (nand_1_out, D, Clk);
  nand nand_2 (nand_2_out, Clk, not_1_out);
  nand nand_3 (Q, nand_1_out, Qcomp);
  nand nand_4 (Qcomp, Q, nand_2_out);
endmodule

module Transparency_ex (
  input  in_1,
  output out_2
);

  wire clock_1_out, dlatch_1_q, dlatch_2_q, dlatch_3_q;

  Clock clock_1 (.out(clock_1_out));
  DLatch dlatch_1 (.D(in_1), .Clk(clock_1_out), .Q(dlatch_1_q));  // open: Qcomp
  DLatch dlatch_2 (.D(dlatch_1_q), .Clk(clock_1_out), .Q(dlatch_2_q));  // open: Qcomp
  DLatch dlatch_3 (.D(dlatch_2_q), .Clk(clock_1_out), .Q(dlatch_3_q));  // open: Qcomp
  DLatch dlatch_4 (.D(dlatch_3_q), .Clk(clock_1_out), .Q(out_2));  // open: Qcomp
endmodule

module SRMSFF (
  input  in_1,
  input  in_2,
  output out_3,
  output out_4
);

  wire clock_1_out, clockedsrlatch_1_q, clockedsrlatch_1_qcomp, not_1_out;

  Clock clock_1 (.out(clock_1_out));
  ClockedSRLatch clockedsrlatch_1 (
    .S(in_1), .Clk(clock_1_out), .R(in_2), .Q(clockedsrlatch_1_q), .Qcomp(clockedsrlatch_1_qcomp));
  not not_1 (not_1_out, clock_1_out);
  ClockedSRLatch clockedsrlatch_2 (
    .S(clockedsrlatch_1_q), .Clk(not_1_out), .R(clockedsrlatch_1_qcomp), .Q(out_3), .Qcomp(out_4));
endmodule

module DFF (
  input  D,
  input  Clk,
  output Q,
  output Qcomp
);

  wire dlatch_1_q, dlatch_1_qcomp, not_1_out, not_2_out;

  not not_1 (not_1_out, Clk);
  DLatch dlatch_1 (.D(D), .Clk(not_1_out), .Q(dlatch_1_q), .Qcomp(dlatch_1_qcomp));
  not not_2 (not_2_out, not_1_out);
  ClockedSRLatch clockedsrlatch_1 (.S(dlatch_1_q), .Clk(not_2_out), .R(dlatch_1_qcomp), .Q(Q), .Qcomp(Qcomp));
endmodule

module TFF (
  input  in_1,
  output out_2,
  output out_3
);

  wire and_1_out, and_2_out, clock_1_out, not_1_out, or_1_out;

  and and_1 (and_1_out, out_2, not_1_out);
  not not_1 (not_1_out, in_1);
  and and_2 (and_2_out, in_1, out_3);
  Clock clock_1 (.out(clock_1_out));
  or or_1 (or_1_out, and_1_out, and_2_out);
  DFF dff_1 (.D(or_1_out), .Clk(clock_1_out), .Q(out_2), .Qcomp(out_3));
endmodule
