// Logisim project lab4_part1.circ as structural Verilog
module dlatch (
  input  D,
  input  Clk,
  output Qa,
  output Qb
);

  wire n7400_1_pin3, n7400_1_pin11, n7404_1_p3;

  // _7404 #(.ShowInternalStructure("true")) 7404_1: pin names not known; wires that end beside it: 1'b1, D, n7404_1_p3, 1'b0, 1'b1
  _7400 #(.ShowInternalStructure("true")) u_7400_1 (
    .pin1(Clk), .pin2(n7404_1_p3), .pin3(n7400_1_pin3), .pin4(n7400_1_pin3), .pin5(Qa), .pin6(Qb),
    .pin13(Clk), .pin12(D), .pin11(n7400_1_pin11), .pin10(n7400_1_pin11), .pin9(Qb), .pin8(Qa));
endmodule

module msflipflop (
  input  D,
  input  Clk,
  output Q
);

  wire dlatch_1_qa, n7404_1_pin12;

  _7404 u_7404_1 (
    .pin13(Clk), .pin12(n7404_1_pin12));  // open: pin1, pin2, pin3, pin4, pin5, pin6, pin11, pin10, pin9, pin8
  dlatch dlatch_1 (.D(D), .Clk(Clk), .Qa(dlatch_1_qa));  // open: Qb
  dlatch dlatch_2 (.D(dlatch_1_qa), .Clk(n7404_1_pin12), .Qa(Q));  // open: Qb
endmodule
