// Logisim project lab4_part3.circ as structural Verilog
module mux2to1 (
  input  x,
  input  y,
  input  s,
  output f
);

  wire and_1_out, and_2_out, not_1_out;

  not not_1 (not_1_out, s);
  and and_1 (and_1_out, x, s);
  and and_2 (and_2_out, y, not_1_out);
  or or_1 (f, and_1_out, and_2_out);
endmodule

module mux4to1 (
  input  x,
  input  w,
  input  s0,
  input  s1,
  input  v,
  input  u,
  output out_7
);

  wire mux2to1_1_f, mux2to1_2_f;

  mux2to1 mux2to1_1 (.x(x), .y(w), .s(s0), .f(mux2to1_1_f));
  mux2to1 mux2to1_2 (.x(v), .y(u), .s(s0), .f(mux2to1_2_f));
  mux2to1 mux2to1_3 (.x(mux2to1_1_f), .y(mux2to1_2_f), .s(s1), .f(out_7));
endmodule

module shifter_bit (
  input  load_val,
  input  brin,
  input  shift,
  input  load_n,
  input  clk,
  input  reset,
  output brout
);

  wire mux2to1_1_f, mux2to1_2_f;

  mux2to1 mux2to1_1 (.x(brin), .y(brout), .s(shift), .f(mux2to1_1_f));
  mux2to1 mux2to1_2 (.x(mux2to1_1_f), .y(load_val), .s(load_n), .f(mux2to1_2_f));
  D_Flip_Flop d_ff_1 (.D(mux2to1_2_f), .clk(clk), .Q(brout), .reset(reset));  // open: Qn, preset
endmodule

module shift_register (
  input  [7:0] LoadVal,
  input  ShiftRight,
  input  Load_n,
  input  clk,
  input  reset,
  input  ASR,
  output [7:0] Q
);

  wire mux2to1_1_f;

  shifter_bit shifter_bit_1 (
    .load_val(LoadVal[0]), .brin(Q[1]), .shift(ShiftRight), .load_n(Load_n), .clk(clk), .reset(reset),
    .brout(Q[0]));
  shifter_bit shifter_bit_2 (
    .load_val(LoadVal[1]), .brin(Q[2]), .shift(ShiftRight), .load_n(Load_n), .clk(clk), .reset(reset),
    .brout(Q[1]));
  shifter_bit shifter_bit_3 (
    .load_val(LoadVal[2]), .brin(Q[3]), .shift(ShiftRight), .load_n(Load_n), .clk(clk), .reset(reset),
    .brout(Q[2]));
  shifter_bit shifter_bit_4 (
    .load_val(LoadVal[3]), .brin(Q[4]), .shift(ShiftRight), .load_n(Load_n), .clk(clk), .reset(reset),
    .brout(Q[3]));
  mux2to1 mux2to1_1 (.x(Q[7]), .y(1'b0), .s(ASR), .f(mux2to1_1_f));
  shifter_bit shifter_bit_5 (
    .load_val(LoadVal[4]), .brin(Q[5]), .shift(ShiftRight), .load_n(Load_n), .clk(clk), .reset(reset),
    .brout(Q[4]));
  shifter_bit shifter_bit_6 (
    .load_val(LoadVal[5]), .brin(Q[6]), .shift(ShiftRight), .load_n(Load_n), .clk(clk), .reset(reset),
    .brout(Q[5]));
  shifter_bit shifter_bit_7 (
    .load_val(LoadVal[6]), .brin(Q[7]), .shift(ShiftRight), .load_n(Load_n), .clk(clk), .reset(reset),
    .brout(Q[6]));
  shifter_bit shifter_bit_8 (
    .load_val(LoadVal[7]), .brin(mux2to1_1_f), .shift(ShiftRight), .load_n(Load_n), .clk(clk), .reset(reset),
    .brout(Q[7]));
endmodule
