// Logisim project Counters_example.circ as structural Verilog
module asynccounter (
  output [3:0] out_1
);

  wire clock_1_out, t_ff_1_qn, t_ff_2_qn, t_ff_3_qn;

  T_Flip_Flop t_ff_1 (.T(1'b1), .clk(clock_1_out), .Q(out_1[0]), .Qn(t_ff_1_qn));  // open: reset, preset
  Clock clock_1 (.out(clock_1_out));
  T_Flip_Flop t_ff_2 (.T(1'b1), .clk(t_ff_1_qn), .Q(out_1[1]), .Qn(t_ff_2_qn));  // open: reset, preset
  T_Flip_Flop t_ff_3 (.T(1'b1), .clk(t_ff_2_qn), .Q(out_1[2]), .Qn(t_ff_3_qn));  // open: reset, preset
  T_Flip_Flop t_ff_4 (.T(1'b1), .clk(t_ff_3_qn), .Q(out_1[3]));  // open: Qn, reset, preset
endmodule

module synccounter (
  output [3:0] out_1
);

  wire and_1_out, and_2_out, and_3_out, clock_1_out;

  T_Flip_Flop t_ff_1 (.T(1'b1), .clk(clock_1_out), .Q(out_1[0]));  // open: Qn, reset, preset
  Clock clock_1 (.out(clock_1_out));
  T_Flip_Flop t_ff_2 (.T(and_1_out), .clk(clock_1_out), .Q(out_1[1]));  // open: Qn, reset, preset
  and and_1 (and_1_out, 1'b1, out_1[0]);
  and and_2 (and_2_out, and_1_out, out_1[1]);
  T_Flip_Flop t_ff_3 (.T(and_2_out), .clk(clock_1_out), .Q(out_1[2]));  // open: Qn, reset, preset
  and and_3 (and_3_out, and_2_out, out_1[2]);
  T_Flip_Flop t_ff_4 (.T(and_3_out), .clk(clock_1_out), .Q(out_1[3]));  // open: Qn, reset, preset
endmodule
