// Logisim project lab5.circ as structural Verilog: 28 circuits, main circuit main
module main (
  input  [3:0] A,
  input  We,
  input  Clk,
  input  [2:0] op
);

  wire hex_decoder_1_s0, hex_decoder_1_s1, hex_decoder_1_s2, hex_decoder_1_s3, hex_decoder_1_s4,
       hex_decoder_1_s5, hex_decoder_1_s6, hex_decoder_2_s0, hex_decoder_2_s1, hex_decoder_2_s2,
       hex_decoder_2_s3, hex_decoder_2_s4, hex_decoder_2_s5, hex_decoder_2_s6, hex_decoder_3_s0,
       hex_decoder_3_s1, hex_decoder_3_s2, hex_decoder_3_s3, hex_decoder_3_s4, hex_decoder_3_s5,
       hex_decoder_3_s6;
  wire [7:0] alu_1_out_4, ALUreg_q;

  HEX_DECODER hex_decoder_1 (
    .SW0(A), .S6(hex_decoder_1_s6), .S5(hex_decoder_1_s5), .S0(hex_decoder_1_s0), .S1(hex_decoder_1_s1),
    .S4(hex_decoder_1_s4), .S3(hex_decoder_1_s3), .S2(hex_decoder_1_s2));
  _7_Segment_Display HEXA (
    .g(hex_decoder_1_s6), .f(hex_decoder_1_s5), .a(hex_decoder_1_s0), .b(hex_decoder_1_s1),
    .e(hex_decoder_1_s4), .d(hex_decoder_1_s3), .c(hex_decoder_1_s2));  // open: dp
  ALU alu_1 (.A(A), .B(ALUreg_q[3:0]), .op(op), .out_4(alu_1_out_4));
  Register ALUreg (.D(alu_1_out_4), .en(We), .clk(Clk), .Q(ALUreg_q));  // open: clr
  HEX_DECODER hex_decoder_2 (
    .SW0(ALUreg_q[3:0]), .S6(hex_decoder_2_s6), .S5(hex_decoder_2_s5), .S0(hex_decoder_2_s0),
    .S1(hex_decoder_2_s1), .S4(hex_decoder_2_s4), .S3(hex_decoder_2_s3), .S2(hex_decoder_2_s2));
  HEX_DECODER hex_decoder_3 (
    .SW0(ALUreg_q[7:4]), .S6(hex_decoder_3_s6), .S5(hex_decoder_3_s5), .S0(hex_decoder_3_s0),
    .S1(hex_decoder_3_s1), .S4(hex_decoder_3_s4), .S3(hex_decoder_3_s3), .S2(hex_decoder_3_s2));
  _7_Segment_Display HEXALU1 (
    .g(hex_decoder_3_s6), .f(hex_decoder_3_s5), .a(hex_decoder_3_s0), .b(hex_decoder_3_s1),
    .e(hex_decoder_3_s4), .d(hex_decoder_3_s3), .c(hex_decoder_3_s2));  // open: dp
  _7_Segment_Display HEXALU0 (
    .g(hex_decoder_2_s6), .f(hex_decoder_2_s5), .a(hex_decoder_2_s0), .b(hex_decoder_2_s1),
    .e(hex_decoder_2_s4), .d(hex_decoder_2_s3), .c(hex_decoder_2_s2));  // open: dp
endmodule

module counter2 (
  input  in_1,
  input  CountEnable,
  input  in_3,
  input  Clock,
  input  Clear,
  input  in_6,
  output [1:0] Q,
  output [1:0] out_8
);

  wire and_1_out;

  T_Flip_Flop TFF0 (.T(in_1), .clk(in_3), .Q(Q[0]), .reset(Clear));  // open: Qn, preset
  // T_Flip_Flop t_ff_1: pin names not known; wires that end beside it: CountEnable, Clock
  and and_1 (and_1_out, in_1, Q[0]);
  T_Flip_Flop TFF1 (.T(and_1_out), .clk(in_3), .Q(Q[1]), .reset(Clear));  // open: Qn, preset
  // AND_Gate and_2 has open pins: out=and_1_out
  T_Flip_Flop t_ff_2 ();  // open: T, clk, Q, Qn, reset, preset
endmodule

module incrementer4 (
  input  CountEnable,
  input  Clock,
  input  Clear,
  output [3:0] Q
);

  wire and_1_out, and_2_out, and_3_out;

  T_Flip_Flop TFF0 (.T(CountEnable), .clk(Clock), .Q(Q[0]), .reset(Clear));  // open: Qn, preset
  and and_1 (and_1_out, CountEnable, Q[0]);
  T_Flip_Flop TFF1 (.T(and_1_out), .clk(Clock), .Q(Q[1]), .reset(Clear));  // open: Qn, preset
  and and_2 (and_2_out, and_1_out, Q[1]);
  T_Flip_Flop TFF2 (.T(and_2_out), .clk(Clock), .Q(Q[2]), .reset(Clear));  // open: Qn, preset
  and and_3 (and_3_out, and_2_out, Q[2]);
  T_Flip_Flop TFF3 (.T(and_3_out), .clk(Clock), .Q(Q[3]), .reset(Clear));  // open: Qn, preset
endmodule

module counter8 (
  input  CountEnable,
  input  Clock,
  input  Clear,
  output [7:0] out_4
);

  wire and_1_out;

  Hex_Digit_Display hex_digit_display_1 (.value(out_4[7:4]));  // open: dp
  Hex_Digit_Display hex_digit_display_2 (.value(out_4[3:0]));  // open: dp
  incrementer4 incrementer4_1 (.CountEnable(CountEnable), .Clock(Clock), .Clear(Clear), .Q(out_4[3:0]));
  and and_1 (and_1_out, out_4[0], out_4[1], out_4[2], out_4[3]);
  incrementer4 incrementer4_2 (.CountEnable(and_1_out), .Clock(Clock), .Clear(Clear), .Q(out_4[7:4]));
endmodule

module handout_example (
  input  Reset,
  input  CountEnable,
  output CounterOut
);

  wire CLK_out, not_1_out, or_1_out;
  wire [3:0] counter_1_q;

  Clock CLK (.out(CLK_out));
  not not_1 (not_1_out, CountEnable);
  or or_1 (or_1_out, CounterOut, not_1_out);
  Counter #(.max('hf), .ongoal("stay"), .width(4)) counter_1 (
    .clr(Reset), .load(or_1_out), .up(1'b1), .clk(CLK_out), .D(4'b0010), .Q(counter_1_q));  // open: count, carry
  and and_1 (CounterOut, counter_1_q[0], counter_1_q[1], counter_1_q[2], counter_1_q[3]);
endmodule

module rate_divider (
  input  Enable,
  input  Clock,
  input  Reset,
  input  [1:0] Rate,
  output DivOut
);

  wire not_1_out, or_1_out;
  wire [7:0] counter_1_q, multiplexer_1_out;

  not not_1 (not_1_out, Enable);
  or or_1 (or_1_out, DivOut, not_1_out);
  Counter #(.ongoal("stay")) counter_1 (
    .clr(Reset), .load(or_1_out), .up(1'b1), .clk(Clock), .D({8{1'b0}}), .Q(counter_1_q));  // open: count, carry
  Multiplexer #(.enable("false"), .select(2), .width(8)) multiplexer_1 (
    .in0(8'h1), .in1(8'h1f), .in2(8'h3f), .in3(8'h7f), .out(multiplexer_1_out), .sel(Rate));
  Comparator comparator_1 (.a(counter_1_q), .b(multiplexer_1_out), .eq(DivOut));  // open: gt, lt
endmodule

module demo_rate_divider (
  input  Clock,
  input  Reset,
  input  [1:0] Rate
);

  wire hex_decoder_1_s0, hex_decoder_1_s1, hex_decoder_1_s2, hex_decoder_1_s3, hex_decoder_1_s4,
       hex_decoder_1_s5, hex_decoder_1_s6, not_1_out, rate_divider_1_divout;
  wire [3:0] DisplayCounter_q;

  rate_divider rate_divider_1 (
    .Enable(1'b1), .Clock(Clock), .Reset(Reset), .Rate(Rate), .DivOut(rate_divider_1_divout));
  not not_1 (not_1_out, rate_divider_1_divout);
  HEX_DECODER hex_decoder_1 (
    .SW0(DisplayCounter_q), .S6(hex_decoder_1_s6), .S5(hex_decoder_1_s5), .S0(hex_decoder_1_s0),
    .S1(hex_decoder_1_s1), .S4(hex_decoder_1_s4), .S3(hex_decoder_1_s3), .S2(hex_decoder_1_s2));
  Counter #(.max('hf), .width(4)) DisplayCounter (
    .clr(Reset), .load(not_1_out), .up(1'b1), .clk(Clock), .D(DisplayCounter_q), .Q(DisplayCounter_q));  // open: count, carry
  _7_Segment_Display HEXA (
    .g(hex_decoder_1_s6), .f(hex_decoder_1_s5), .a(hex_decoder_1_s0), .b(hex_decoder_1_s1),
    .e(hex_decoder_1_s4), .d(hex_decoder_1_s3), .c(hex_decoder_1_s2));  // open: dp
endmodule

module MORSE_LUT (
  input  [2:0] Char,
  output [13:0] MorseCode
);

  Multiplexer #(.enable("false"), .select(3), .width(14)) multiplexer_1 (
    .in0(14'h2a00), .in1(14'h3800), .in2(14'h2b80), .in3(14'h2ae0), .in4(14'h2ee0), .in5(14'h3ab8),
    .in6(14'h3aee), .in7(14'h3ba8), .out(MorseCode), .sel(Char));
endmodule

module morse_code (
  input  [2:0] CharSelect,
  input  LoadEnable,
  input  Enable
);

  wire Clk_out, rate_divider_1_divout, undriven;
  wire [13:0] morse_lut_1_morsecode;

  Clock Clk (.out(Clk_out));
  rate_divider rate_divider_1 (.Enable(Enable), .Clock(Clk_out), .DivOut(rate_divider_1_divout));  // open: Reset, Rate
  MORSE_LUT morse_lut_1 (.Char(CharSelect), .MorseCode(morse_lut_1_morsecode));
  // Shift_Register #(.length(14)) shift_register_1: pin names not known; wires that end beside it: LoadEnable, rate_divider_1_divout, Clk_out, 1'b0, morse_lut_1_morsecode[0], morse_lut_1_morsecode[1], morse_lut_1_morsecode[2], morse_lut_1_morsecode[3], morse_lut_1_morsecode[4], morse_lut_1_morsecode[5], morse_lut_1_morsecode[6], morse_lut_1_morsecode[7], morse_lut_1_morsecode[8], morse_lut_1_morsecode[9], morse_lut_1_morsecode[10], morse_lut_1_morsecode[11]
  LED led_1 (.in(undriven));
endmodule

module full_adder (
  input  Cin,
  input  A,
  input  B,
  output Cout,
  output S
);

  wire and_1_out, and_2_out, xor_1_out;

  and and_1 (and_1_out, B, A);
  xor xor_1 (xor_1_out, A, B);
  and and_2 (and_2_out, xor_1_out, Cin);
  xor xor_2 (S, Cin, xor_1_out);
  or or_1 (Cout, and_2_out, and_1_out);
endmodule

module ripple_carry4 (
  input  [3:0] A,
  input  [3:0] B,
  input  Cin,
  output Cout,
  output [3:0] S
);

  wire full_adder_1_cout, full_adder_2_cout, full_adder_3_cout;

  full_adder full_adder_1 (.Cin(Cin), .A(A[0]), .B(B[0]), .Cout(full_adder_1_cout), .S(S[0]));
  full_adder full_adder_2 (.Cin(full_adder_1_cout), .A(A[1]), .B(B[1]), .Cout(full_adder_2_cout), .S(S[1]));
  full_adder full_adder_3 (.Cin(full_adder_2_cout), .A(A[2]), .B(B[2]), .Cout(full_adder_3_cout), .S(S[2]));
  full_adder full_adder_4 (.Cin(full_adder_3_cout), .A(A[3]), .B(B[3]), .Cout(Cout), .S(S[3]));
endmodule

module op0 (
  input  [3:0] A,
  output [7:0] OPout
);

  wire full_adder_1_cout, full_adder_2_cout, full_adder_3_cout, full_adder_4_cout, full_adder_5_cout,
       full_adder_6_cout, full_adder_7_cout;

  full_adder full_adder_1 (.Cin(1'b1), .A(A[0]), .Cout(full_adder_1_cout), .S(OPout[0]));  // open: B
  full_adder full_adder_2 (.Cin(full_adder_1_cout), .A(A[1]), .Cout(full_adder_2_cout), .S(OPout[1]));  // open: B
  full_adder full_adder_3 (.Cin(full_adder_2_cout), .A(A[2]), .Cout(full_adder_3_cout), .S(OPout[2]));  // open: B
  full_adder full_adder_4 (.Cin(full_adder_3_cout), .A(A[3]), .Cout(full_adder_4_cout), .S(OPout[3]));  // open: B
  full_adder full_adder_5 (.Cin(full_adder_4_cout), .Cout(full_adder_5_cout), .S(OPout[4]));  // open: A, B
  full_adder full_adder_6 (.Cin(full_adder_5_cout), .Cout(full_adder_6_cout), .S(OPout[5]));  // open: A, B
  full_adder full_adder_7 (.Cin(full_adder_6_cout), .Cout(full_adder_7_cout), .S(OPout[6]));  // open: A, B
  full_adder full_adder_8 (.Cin(full_adder_7_cout), .Cout(OPout[7]));  // open: A, B, S
endmodule

module op1 (
  input  [3:0] A,
  input  [3:0] B,
  output [7:0] OPout
);

  wire full_adder_1_cout, full_adder_2_cout, full_adder_3_cout, full_adder_4_cout, full_adder_5_cout,
       full_adder_6_cout, full_adder_7_cout;

  full_adder full_adder_1 (.A(A[0]), .B(B[0]), .Cout(full_adder_1_cout), .S(OPout[0]));  // open: Cin
  full_adder full_adder_2 (.Cin(full_adder_1_cout), .A(A[1]), .B(B[1]), .Cout(full_adder_2_cout), .S(OPout[1]));
  full_adder full_adder_3 (.Cin(full_adder_2_cout), .A(A[2]), .B(B[2]), .Cout(full_adder_3_cout), .S(OPout[2]));
  full_adder full_adder_4 (.Cin(full_adder_3_cout), .A(A[3]), .B(B[3]), .Cout(full_adder_4_cout), .S(OPout[3]));
  full_adder full_adder_5 (.Cin(full_adder_4_cout), .Cout(full_adder_5_cout), .S(OPout[4]));  // open: A, B
  full_adder full_adder_6 (.Cin(full_adder_5_cout), .Cout(full_adder_6_cout), .S(OPout[5]));  // open: A, B
  full_adder full_adder_7 (.Cin(full_adder_6_cout), .Cout(full_adder_7_cout), .S(OPout[6]));  // open: A, B
  full_adder full_adder_8 (.Cin(full_adder_7_cout), .S(OPout[7]));  // open: A, B, Cout
endmodule

module op2 (
  input  [3:0] A,
  input  [3:0] B,
  output [7:0] OPout
);

  wire [7:0] bit_extender_1_out, bit_extender_2_out;

  assign bit_extender_1_out = {{4{1'b0}}, A};  // Bit_Extender bit_extender_1
  assign bit_extender_2_out = {{4{1'b0}}, B};  // Bit_Extender bit_extender_2
  Adder adder_1 (.a(bit_extender_1_out), .b(bit_extender_2_out), .out(OPout));  // open: cin, cout
endmodule

module op3 (
  input  [3:0] A,
  input  [3:0] B,
  output [7:0] OPout
);

  or or_1 (OPout[4], A[0], B[0]);
  xor xor_1 (OPout[0], A[0], B[0]);
  or or_2 (OPout[5], A[1], B[1]);
  xor xor_2 (OPout[1], A[1], B[1]);
  or or_3 (OPout[6], A[2], B[2]);
  xor xor_3 (OPout[2], A[2], B[2]);
  or or_4 (OPout[7], A[3], B[3]);
  xor xor_4 (OPout[3], A[3], B[3]);
endmodule

module op4 (
  input  [3:0] A,
  input  [3:0] B,
  output [7:0] OPout
);

  or or_1 (OPout[0], A[0], A[1], A[2], A[3], B[0], B[1], B[2], B[3]);

  assign OPout[7:1] = {7{1'b0}};
endmodule

module op5 (
  input  [3:0] A,
  input  [3:0] B,
  output [7:0] OPout
);

  wire [2:0] bit_extender_2_out;
  wire [7:0] bit_extender_1_out, shifter_1_out;
  wire [7:7] shifter_2_out;

  assign bit_extender_1_out = {{4{B[3]}}, B};  // Bit_Extender bit_extender_1
  Shifter shifter_1 (.in(bit_extender_1_out), .\dist (A[2:0]), .out(shifter_1_out));
  Shifter shifter_2 (.in(shifter_1_out), .\dist (bit_extender_2_out), .out({shifter_2_out[7], OPout[6:0]}));
  assign bit_extender_2_out = {{2{A[3]}}, A[3]};  // Bit_Extender bit_extender_2
  Multiplier #(.width(1)) multiplier_1 (
    .a(shifter_2_out[7]), .b(A[3]), .out(OPout[7]), .cin(shifter_2_out[7]));  // open: cout
endmodule

module op6 (
  input  [3:0] A,
  input  [3:0] B,
  output [7:0] OPout
);

  wire [0:0] shifter_2_out;
  wire [2:0] bit_extender_2_out;
  wire [7:0] bit_extender_1_out, shifter_1_out;

  assign bit_extender_1_out = {{4{B[3]}}, B};  // Bit_Extender bit_extender_1
  Shifter #(.shift("lr")) shifter_1 (.in(bit_extender_1_out), .\dist (A[2:0]), .out(shifter_1_out));
  Shifter #(.shift("lr")) shifter_2 (
    .in(shifter_1_out), .\dist (bit_extender_2_out), .out({OPout[7:1], shifter_2_out[0]}));
  assign bit_extender_2_out = {{2{A[3]}}, A[3]};  // Bit_Extender bit_extender_2
  Multiplier #(.width(1)) multiplier_1 (
    .a(shifter_2_out[0]), .b(A[3]), .out(OPout[0]), .cin(shifter_2_out[0]));  // open: cout
endmodule

module op7 (
  input  [3:0] A,
  input  [3:0] B,
  output [7:0] OPout
);

  wire [7:0] bit_extender_1_out, bit_extender_2_out;

  assign bit_extender_1_out = {{4{1'b0}}, A};  // Bit_Extender bit_extender_1
  assign bit_extender_2_out = {{4{1'b0}}, B};  // Bit_Extender bit_extender_2
  Multiplier multiplier_1 (.a(bit_extender_1_out), .b(bit_extender_2_out), .out(OPout));  // open: cin, cout
endmodule

module ALU (
  input  [3:0] A,
  input  [3:0] B,
  input  [2:0] op,
  output [7:0] out_4
);

  wire [7:0] op0_1_opout, op1_1_opout, op2_1_opout, op3_1_opout, op4_1_opout, op5_1_opout, op6_1_opout,
       op7_1_opout;

  op0 op0_1 (.A(A), .OPout(op0_1_opout));
  op1 op1_1 (.A(A), .B(B), .OPout(op1_1_opout));
  op2 op2_1 (.A(A), .B(B), .OPout(op2_1_opout));
  op3 op3_1 (.A(A), .B(B), .OPout(op3_1_opout));
  op4 op4_1 (.A(A), .B(B), .OPout(op4_1_opout));
  op5 op5_1 (.A(A), .B(B), .OPout(op5_1_opout));
  op6 op6_1 (.A(B), .B(A), .OPout(op6_1_opout));
  op7 op7_1 (.A(A), .B(B), .OPout(op7_1_opout));
  Multiplexer #(.enable("false"), .select(3), .width(8)) multiplexer_1 (
    .in0(op0_1_opout), .in1(op1_1_opout), .in2(op2_1_opout), .in3(op3_1_opout), .in4(op4_1_opout),
    .in5(op5_1_opout), .in6(op6_1_opout), .in7(op7_1_opout), .out(out_4), .sel(op));
endmodule

module HEX0 (
  input  D3,
  input  D2,
  input  D1,
  input  D0,
  output S0
);

  wire and_1_out, and_2_out, and_3_out, and_4_out, and_5_out, not_1_out, not_2_out, not_3_out, not_4_out;

  not not_1 (not_1_out, D3);
  not not_2 (not_2_out, D2);
  not not_3 (not_3_out, D1);
  not not_4 (not_4_out, D0);
  and and_1 (and_1_out, not_2_out, not_4_out);
  and and_2 (and_2_out, not_1_out, D1);
  and and_3 (and_3_out, not_1_out, D2, D0);
  and and_4 (and_4_out, D2, D1);
  and and_5 (and_5_out, D3, not_2_out, not_3_out);
  or or_1 (S0, and_1_out, and_2_out, and_3_out, and_4_out, and_5_out);
endmodule

module HEX1 (
  input  D3,
  input  D2,
  input  D1,
  input  D0,
  output S1
);

  wire and_1_out, and_2_out, and_3_out, and_4_out, and_5_out, not_1_out, not_2_out, not_3_out, not_4_out;

  not not_1 (not_1_out, D3);
  not not_2 (not_2_out, D2);
  not not_3 (not_3_out, D1);
  not not_4 (not_4_out, D0);
  and and_1 (and_1_out, not_1_out, not_2_out);
  and and_2 (and_2_out, not_1_out, not_3_out, not_4_out);
  and and_3 (and_3_out, not_2_out, not_4_out);
  and and_4 (and_4_out, not_1_out, D1, D0);
  and and_5 (and_5_out, D3, not_3_out, D0);
  or or_1 (S1, and_1_out, and_2_out, and_3_out, and_4_out, and_5_out);
endmodule

module HEX2 (
  input  D3,
  input  D2,
  input  D1,
  input  D0,
  output S2
);

  wire and_1_out, and_2_out, and_3_out, and_4_out, and_5_out, not_1_out, not_2_out, not_3_out;

  not not_1 (not_1_out, D3);
  not not_2 (not_2_out, D2);
  not not_3 (not_3_out, D1);
  and and_1 (and_1_out, not_1_out, not_3_out);
  and and_2 (and_2_out, not_1_out, D0);
  and and_3 (and_3_out, not_3_out, D0);
  and and_4 (and_4_out, not_1_out, D2);
  and and_5 (and_5_out, D3, not_2_out);
  or or_1 (S2, and_1_out, and_2_out, and_3_out, and_4_out, and_5_out);
endmodule

module HEX3 (
  input  D3,
  input  D2,
  input  D1,
  input  D0,
  output S3
);

  wire and_1_out, and_2_out, and_3_out, and_4_out, and_5_out, and_6_out, not_1_out, not_2_out, not_3_out,
       not_4_out;

  not not_1 (not_1_out, D3);
  not not_2 (not_2_out, D2);
  not not_3 (not_3_out, D1);
  not not_4 (not_4_out, D0);
  and and_1 (and_1_out, not_1_out, not_2_out, not_4_out);
  and and_2 (and_2_out, not_1_out, D1, not_4_out);
  and and_3 (and_3_out, not_2_out, D1, D0);
  and and_4 (and_4_out, D2, not_3_out, D0);
  and and_5 (and_5_out, D3, not_3_out);
  and and_6 (and_6_out, D3, D2, not_4_out);
  or or_1 (S3, and_1_out, and_2_out, and_3_out, and_4_out, and_5_out, and_6_out);
endmodule

module HEX4 (
  input  D3,
  input  D2,
  input  D1,
  input  D0,
  output S4
);

  wire and_1_out, and_2_out, and_3_out, and_4_out, not_1_out, not_2_out;

  not not_1 (not_1_out, D2);
  not not_2 (not_2_out, D0);
  and and_1 (and_1_out, not_1_out, not_2_out);
  and and_2 (and_2_out, D1, not_2_out);
  and and_3 (and_3_out, D3, D1);
  and and_4 (and_4_out, D3, D2);
  or or_1 (S4, and_1_out, and_2_out, and_3_out, and_4_out);
endmodule

module HEX5 (
  input  D3,
  input  D2,
  input  D1,
  input  D0,
  output S5
);

  wire and_1_out, and_2_out, and_3_out, and_4_out, and_5_out, not_1_out, not_2_out, not_3_out, not_4_out;

  not not_1 (not_1_out, D3);
  not not_2 (not_2_out, D2);
  not not_3 (not_3_out, D1);
  not not_4 (not_4_out, D0);
  and and_1 (and_1_out, not_1_out, not_3_out, not_4_out);
  and and_2 (and_2_out, not_1_out, D2, not_3_out);
  and and_3 (and_3_out, not_1_out, D2, not_4_out);
  and and_4 (and_4_out, D3, not_2_out);
  and and_5 (and_5_out, D3, D1);
  or or_1 (S5, and_1_out, and_2_out, and_3_out, and_4_out, and_5_out);
endmodule

module HEX6 (
  input  D3,
  input  D2,
  input  D1,
  input  D0,
  output S6
);

  wire and_1_out, and_2_out, and_3_out, not_1_out, not_2_out, not_3_out;

  not not_1 (not_1_out, D2);
  not not_2 (not_2_out, D1);
  not not_3 (not_3_out, D0);
  and and_1 (and_1_out, not_1_out, D1);
  and and_2 (and_2_out, D2, not_2_out);
  and and_3 (and_3_out, D2, not_3_out);
  or or_1 (S6, and_1_out, and_2_out, and_3_out, D3);
endmodule

module HEX_DECODER (
  input  [3:0] SW0,
  output S6,
  output S5,
  output S0,
  output S1,
  output S4,
  output S3,
  output S2
);

  HEX4 hex4_1 (.D3(SW0[3]), .D2(SW0[2]), .D1(SW0[1]), .D0(SW0[0]), .S4(S4));
  HEX6 hex6_1 (.D3(SW0[3]), .D2(SW0[2]), .D1(SW0[1]), .D0(SW0[0]), .S6(S6));
  HEX3 hex3_1 (.D3(SW0[3]), .D2(SW0[2]), .D1(SW0[1]), .D0(SW0[0]), .S3(S3));
  HEX5 hex5_1 (.D3(SW0[3]), .D2(SW0[2]), .D1(SW0[1]), .D0(SW0[0]), .S5(S5));
  HEX2 hex2_1 (.D3(SW0[3]), .D2(SW0[2]), .D1(SW0[1]), .D0(SW0[0]), .S2(S2));
  HEX0 hex0_1 (.D3(SW0[3]), .D2(SW0[2]), .D1(SW0[1]), .D0(SW0[0]), .S0(S0));
  HEX1 hex1_1 (.D3(SW0[3]), .D2(SW0[2]), .D1(SW0[1]), .D0(SW0[0]), .S1(S1));
endmodule
