// Logisim project lab6_part1.circ as structural Verilog
module part_1_state_table (
  input  [2:0] curr_state,
  input  w,
  output [2:0] next_state
);

  wire and_1_out, and_2_out, and_3_out, and_4_out, and_5_out, and_6_out, and_7_out, not_1_out, not_2_out,
       not_3_out, not_4_out;

  not not_1 (not_1_out, curr_state[2]);
  not not_2 (not_2_out, curr_state[1]);
  not not_3 (not_3_out, curr_state[0]);
  not not_4 (not_4_out, w);
  or or_1 (next_state[2], not_4_out, curr_state[1]);
  and and_1 (and_1_out, not_1_out, not_3_out);
  or or_2 (next_state[1], and_1_out, and_2_out);
  and and_2 (and_2_out, curr_state[1], curr_state[0]);
  and and_3 (and_3_out, not_1_out, not_3_out, w);
  and and_4 (and_4_out, not_2_out, curr_state[0], not_4_out);
  and and_5 (and_5_out, curr_state[1], curr_state[0], w);
  and and_6 (and_6_out, curr_state[2], not_3_out, not_4_out);
  and and_7 (and_7_out, curr_state[2], not_2_out, curr_state[0]);
  or or_3 (next_state[0], and_3_out, and_4_out, and_5_out, and_6_out, and_7_out);
endmodule

module part_1_FSM (
  input  W,
  input  Enable,
  input  Reset,
  output z
);

  wire and_1_out, and_2_out, Clk_out, not_1_out, not_2_out;
  wire [2:0] state_q, state_table_next_state;

  part_1_state_table state_table (.curr_state(state_q), .w(W), .next_state(state_table_next_state));
  Register #(.width(3)) state (.D(state_table_next_state), .en(Enable), .clk(Clk_out), .Q(state_q), .clr(Reset));
  Clock Clk (.out(Clk_out));
  not not_1 (not_1_out, state_q[0]);
  not not_2 (not_2_out, state_q[1]);
  and and_1 (and_1_out, state_q[0], state_q[1], state_q[2]);
  and and_2 (and_2_out, not_1_out, not_2_out, state_q[2]);
  or or_1 (z, and_1_out, and_2_out);

  // Notes on the sheet:
  //   your state table
  //   state register
  //   output logic (to be completed by you)
endmodule
