// Logisim project lab7_part1.circ as structural Verilog: 1 circuit, main circuit main
module main (
  input  in_1,
  input  in_2,
  input  in_3,
  input  in_4
);

  wire clock_1_out, nor_1_out;
  wire [3:0] counter_1_q, ram_1_dout;
  wire [4:4] t_ff_1_q;

  Clock clock_1 (.out(clock_1_out));
  Counter #(.max('hf), .width(4)) counter_1 (
    .clr(in_2), .load(in_4), .clk(clock_1_out), .Q(counter_1_q));  // open: up, count, D, carry
  nor nor_1 (nor_1_out, counter_1_q[0], counter_1_q[1], counter_1_q[2], counter_1_q[3]);
  T_Flip_Flop t_ff_1 (.T(nor_1_out), .clk(nor_1_out), .Q(t_ff_1_q[4]));  // open: Qn, reset, preset
  RAM #(.addrWidth(5), .dataWidth(4)) ram_1 (
    .addr({t_ff_1_q[4], counter_1_q}), .we(in_1), .oe(in_3), .clk(clock_1_out), .din(counter_1_q),
    .dout(ram_1_dout));
  Hex_Digit_Display hex_digit_display_1 (.value(ram_1_dout));  // open: dp
endmodule
