// Logisim project lab7_part2.circ as structural Verilog: 6 circuits, main circuit main
module main (
  input  Reset,
  input  [6:0] X,
  input  [6:0] Y,
  input  Enable
);

  wire clock_1_out, controlunit_1_r, controlunit_1_writeenable, rgb_video_1_p3;
  wire [6:0] rgb_video_1_p4, rgb_video_1_p5;
  wire [23:0] controlunit_1_d, rgb_video_1_p6;

  Clock clock_1 (.out(clock_1_out));
  ControlUnit controlunit_1 (
    .Clk(clock_1_out), .Reset(Reset), .Enable(Enable), .D(controlunit_1_d), .R(controlunit_1_r),
    .WriteEnable(controlunit_1_writeenable));
  // RGB_Video rgb_video_1: pin names not known; wires that end beside it: Reset, clock_1_out, rgb_video_1_p3, rgb_video_1_p4, rgb_video_1_p5, rgb_video_1_p6
  Datapath datapath_1 (
    .X(X), .Y(Y), .WriteEnable(controlunit_1_writeenable), .Clk(clock_1_out), .Reset(controlunit_1_r),
    .Data(controlunit_1_d), .We(rgb_video_1_p3), .X_coord(rgb_video_1_p4), .Y_coord(rgb_video_1_p5),
    .out_10(rgb_video_1_p6));
endmodule

module ControlUnit (
  input  Clk,
  input  Reset,
  input  Enable,
  output [23:0] D,
  output R,
  output WriteEnable
);

  wire register_1_q, state_table_1_nextstate;

  state_table state_table_1 (
    .Reset(Reset), .curr(register_1_q), .E(Enable), .Colour(D), .nextstate(state_table_1_nextstate),
    .Enable(WriteEnable));
  Register #(.width(1)) register_1 (.D(state_table_1_nextstate), .clk(Clk), .Q(register_1_q), .clr(Reset));  // open: en

  assign R = Reset;
endmodule

module Datapath (
  input  [6:0] X,
  input  [6:0] Y,
  input  WriteEnable,
  input  Clk,
  input  Reset,
  input  [23:0] Data,
  output We,
  output [6:0] X_coord,
  output [6:0] Y_coord,
  output [23:0] out_10
);

  wire comparator_1_eq;
  wire [3:0] counter_1_q, counter_2_q;
  wire [6:0] bit_extender_1_out, bit_extender_2_out;

  Counter #(.max('hf), .width(4)) counter_1 (
    .clr(Reset), .clk(Clk), .D(counter_1_q), .Q(counter_1_q));  // open: load, up, count, carry
  Comparator #(.width(4)) comparator_1 (.a(counter_1_q), .b(4'b0000), .eq(comparator_1_eq));  // open: gt, lt
  assign bit_extender_1_out = {{3{1'b0}}, counter_1_q};  // Bit_Extender bit_extender_1
  Counter #(.max('hf), .width(4)) counter_2 (
    .clr(Reset), .clk(comparator_1_eq), .D(counter_2_q), .Q(counter_2_q));  // open: load, up, count, carry
  Adder #(.width(7)) adder_1 (.a(bit_extender_1_out), .b(X), .out(X_coord));  // open: cin, cout
  assign bit_extender_2_out = {{3{1'b0}}, counter_2_q};  // Bit_Extender bit_extender_2
  Adder #(.width(7)) adder_2 (.a(bit_extender_2_out), .b(Y), .out(Y_coord));  // open: cin, cout

  assign out_10 = Data;
  assign We = WriteEnable;
endmodule

module state_table (
  input  Reset,
  input  curr,
  input  E,
  output [23:0] Colour,
  output nextstate,
  output Enable
);

  colour_state colour_state_1 (.Reset(Reset), .curr_state(curr), .Colour(Colour));
  next_state next_state_1 (.a(curr), .x(nextstate));

  assign Enable = E;
endmodule

module next_state (
  input  a,
  output x
);

  not not_1 (x, a);
endmodule

module colour_state (
  input  Reset,
  input  curr_state,
  output [23:0] Colour
);

  wire and_1_out, comparator_1_eq;
  wire [1:0] t_ff_1_q;
  wire [2:0] counter_1_q;

  Counter #(.max('h7), .width(3)) counter_1 (
    .clr(Reset), .clk(curr_state), .Q(counter_1_q));  // open: load, up, count, D, carry
  Comparator #(.width(3)) comparator_1 (.a(3'b011), .b(counter_1_q), .eq(comparator_1_eq));  // open: gt, lt
  T_Flip_Flop t_ff_1 (.T(comparator_1_eq), .clk(curr_state), .Q(t_ff_1_q[0]), .reset(Reset));  // open: Qn, preset
  and and_1 (and_1_out, comparator_1_eq, t_ff_1_q[0]);
  T_Flip_Flop t_ff_2 (.T(and_1_out), .clk(curr_state), .Q(t_ff_1_q[1]), .reset(Reset));  // open: Qn, preset
  Multiplexer #(.enable("false"), .select(2), .width(24)) multiplexer_1 (
    .in0(24'h36535), .in1(24'hff00ff), .in2(24'hff00), .in3(24'hffff00), .out(Colour), .sel(t_ff_1_q));
endmodule
